// Logisim project cpu.circ as structural Verilog: 1 circuit, main circuit main
module main (
);

  wire [7:0] undriven, undriven_2;

  LED led_1 (.in(undriven[7]));
  LED led_2 (.in(undriven[6]));
  LED led_3 (.in(undriven[5]));
  LED led_4 (.in(undriven[4]));
  LED led_5 (.in(undriven[3]));
  LED led_6 (.in(undriven[2]));
  LED led_7 (.in(undriven[1]));
  LED led_8 (.in(undriven[0]));
  LED led_9 (.in(undriven_2[7]));
  LED led_10 (.in(undriven_2[6]));
  LED led_11 (.in(undriven_2[5]));
  LED led_12 (.in(undriven_2[4]));
  LED led_13 (.in(undriven_2[3]));
  LED led_14 (.in(undriven_2[2]));
  LED led_15 (.in(undriven_2[1]));
  LED led_16 (.in(undriven_2[0]));
endmodule
